# Fritzing sketch Schematic (saved by Fritzing 0.5.2b)
breadboards: 1

parts:
  Arduino1 = Arduino
  Front_Panel_LED = RGB LED - (4 legs)
  Buzzy_Speaker = Loudspeaker
  R1_100ohm = Resistor [resistance=100 package=THT]
  Knob_Pot_10K = Trimmer Potentiometer [package=THT]
  Bluetooth = mystery part, 13 pins [chip_label=? spacing=300mil]
  R4_82ohm = Resistor [resistance=100 package=THT]
  R3_47_ohm = Resistor [resistance=47 package=THT]
  R2_47ohm = Resistor [resistance=47 package=THT]
  Vin_DC_Jack_-_12v = female pin header, 2 pins [form="♀ (female)"]
  Q1 = Basic FET N-Channel [package="TO220 [THT]"]
  Panel_Meter_-_0-10v_DC_display = mystery part, 2 pins [chip_label=? spacing=300mil]

nets:
  GND: Arduino1.GND, Front_Panel_LED.connector1, Buzzy_Speaker.pin2, Knob_Pot_10K.leg1, Bluetooth.pin13, Vin_DC_Jack_-_12v.pin2, Q1.source
  N1: Arduino1.D11, R4_82ohm.Pin_1
  N2: Arduino1.D10, R3_47_ohm.Pin_1
  N3: Arduino1.D9, R2_47ohm.Pin_1
  N4: Arduino1.D6, Q1.gate
  N5: Arduino1.D3, Bluetooth.pin1
  N6: Arduino1.D2, Bluetooth.pin2
  N7: Arduino1.3V3, Bluetooth.pin12
  N8: Arduino1.+5V, Knob_Pot_10K.leg2
  N9: Arduino1.VIN, Vin_DC_Jack_-_12v.pin1, Panel_Meter_-_0-10v_DC_display.pin1
  N10: Arduino1.A0, Knob_Pot_10K.wiper
  N11: Front_Panel_LED.connector0, R4_82ohm.Pin_0
  N12: Front_Panel_LED.connector2, R3_47_ohm.Pin_0
  N13: Front_Panel_LED.connector3, R2_47ohm.Pin_0
  N14: Buzzy_Speaker.pin1, R1_100ohm.Pin_0
  N15: Q1.drain, Panel_Meter_-_0-10v_DC_display.pin2

notes:
  (The BT modules are actually a 34-pin package with pins on 3 sides, However, all the connections we want for this project (RX,TX,Vcc,Gnd) are on the LHS of the module and these are the pins marked here.)
